# Fritzing sketch Schematic (saved by Fritzing 0.8.5b)
circuit board: 5.72571cm x 3.2324cm
breadboards: 1

parts:
  part = Arduino Nano (Rev3.0)
  PWR = Battery block 9V
  TURRET_MTR = DC Motor
  WALK_MTR = DC Motor
  BLUE_TOOTH = mystery part, 4 pins [chip_label=?]  # not connected

nets:
  N1: part.D5, TURRET_MTR.pin_2
  N2: part.D6, TURRET_MTR.pin_1
  N3: part.D7, WALK_MTR.pin_1
  N4: part.D8, WALK_MTR.pin_2
  N5: part.VIN, PWR.+
  N6: part.GND, PWR.-
